// Logisim project TinyCPU.circ as structural Verilog: 5 circuits, main circuit TinyCPU
module TinyCPU (
);

  Datapath datapath_1 ();  // open: DATA_IN, ACC_LOAD, VALID_IN, CLK, out_5, out_6
  AddressPath addresspath_1 ();  // open: ADDRESS_IN, AR_LOAD, VALID_IN, CLK, ADDRESS, out_6
  Memory memory_1 ();
  ErrorFlags errorflags_1 ();

  // Notes on the sheet:
  //   TinyCPU 16/12 starter — wire and verify each subcircuit before adding control logic
endmodule

module Datapath (
  input  [15:0] DATA_IN,
  input  ACC_LOAD,
  input  VALID_IN,
  input  CLK,
  output [15:0] out_5,
  output out_6
);

  Register #(.width(16)) ACC ();  // open: D, en, clk, Q, clr
  Register #(.width(1)) ACC_VALID ();  // open: D, en, clk, Q, clr

  // Notes on the sheet:
  //   16-bit accumulator plus validity state
endmodule

module AddressPath (
  input  [11:0] ADDRESS_IN,
  input  AR_LOAD,
  input  VALID_IN,
  input  CLK,
  output [11:0] ADDRESS,
  output out_6
);

  Register #(.width(12)) AR ();  // open: D, en, clk, Q, clr
  Register #(.width(1)) AR_VALID ();  // open: D, en, clk, Q, clr

  // Notes on the sheet:
  //   12-bit unsigned address register plus validity state
endmodule

module Memory (
);

  RAM #(.addrWidth(12), .dataWidth(16)) DATA_RAM ();  // open: addr, we, oe, clk, din, dout
  RAM #(.addrWidth(12), .dataWidth(1)) VALID_RAM ();  // open: addr, we, oe, clk, din, dout

  // Notes on the sheet:
  //   Parallel value/valid RAM — shared address and write-enable are the next wiring step
endmodule

module ErrorFlags (
);

  Register #(.width(1)) OVF ();  // open: D, en, clk, Q, clr
  Register #(.width(1)) INV ();  // open: D, en, clk, Q, clr
  Register #(.width(1)) DIV0 ();  // open: D, en, clk, Q, clr
  Register #(.width(1)) ILL ();  // open: D, en, clk, Q, clr
  Register #(.width(1)) ADDR ();  // open: D, en, clk, Q, clr
  Register #(.width(1)) INPUT ();  // open: D, en, clk, Q, clr

  // Notes on the sheet:
  //   Sticky set-dominant error state; CLEAR_ERROR must be the sole clear source
endmodule
