// Logisim project TinyCPU-FetchDecode.circ as structural Verilog: 1 circuit, main circuit FetchDecode
module FetchDecode (
  input  DEC_JUMP_NOT_ZERO,
  input  NOT_ZERO,
  input  CLK,
  input  RESET,
  input  [15:0] PROGRAM_LIMIT,
  input  DEC_HALT_ERROR,
  output JUMP_NOT_ZERO,
  output HALT_ERROR,
  output [11:0] PC_OUT,
  output [21:0] OPCODE
);

  wire PC_RANGE_gt;
  wire [15:0] adder_1_out, NEXT_PC_out, undriven;
  wire [15:12] PC_q;

  Register #(.width(16)) PC (.D(NEXT_PC_out), .en(1'b1), .clk(CLK), .Q({PC_q, PC_OUT}), .clr(RESET));
  Adder #(.width(16)) adder_1 (.a({PC_q, PC_OUT}), .b(16'h1), .out(adder_1_out));  // open: cin, cout
  Comparator #(.width(16)) PC_RANGE (.a({PC_q, PC_OUT}), .b(PROGRAM_LIMIT), .gt(PC_RANGE_gt));  // open: eq, lt
  ROM #(.addrWidth(12), .dataWidth(22)) INSTRUCTION_ROM (.addr(PC_OUT), .data(OPCODE));
  Multiplexer #(.width(16)) NEXT_PC (.in0(adder_1_out), .in1(undriven), .out(NEXT_PC_out), .sel(JUMP_NOT_ZERO));
  and JNZ_TAKEN (JUMP_NOT_ZERO, DEC_JUMP_NOT_ZERO, NOT_ZERO);
  or ERROR_HALT (HALT_ERROR, PC_RANGE_gt, DEC_HALT_ERROR);

  // Notes on the sheet:
  //   PROGRAM_LIMIT: initial=0xfff
  //   AP 7 machine format v1: stable six-bit opcode allocation and encoder-generated ROM
  //   contents of INSTRUCTION_ROM (hex, n*v repeats v):
  //   ffff 1c0065 3 1c0064 2a0000 50065 1c0064 240004 2c0000
endmodule
